// Logisim project Proj2starter.circ as structural Verilog: 5 circuits, main circuit regfile
module CPUmain (
  input  [31:0] in_1
);

  wire control_1_imm_sel, regfile_1_p2;
  wire [3:0] control_1_alu_code;
  wire [4:0] regfile_1_p3, regfile_1_p4, regfile_1_p5;
  wire [31:0] control_1_imm, multiplexer_1_out, regfile_1_p1, regfile_1_p6, regfile_1_p7;

  // regfile regfile_1: pin names not known; wires that end beside it: regfile_1_p1, regfile_1_p2, regfile_1_p3, regfile_1_p4, regfile_1_p5, regfile_1_p6, regfile_1_p7
  Control control_1 (
    .Inst(in_1), .rs(regfile_1_p4), .rt(regfile_1_p5), .rd(regfile_1_p3), .imm(control_1_imm),
    .reg_write_e(regfile_1_p2), .imm_sel(control_1_imm_sel), .ALU_code(control_1_alu_code));
  Multiplexer #(.width(32)) multiplexer_1 (
    .in0(regfile_1_p7), .in1(control_1_imm), .out(multiplexer_1_out), .sel(control_1_imm_sel));
  Bit_Extender bit_extender_1 ();  // open: in, out
  ALU alu_1 (.OP2(multiplexer_1_out), .OP1(regfile_1_p6), .ALU_CODE(control_1_alu_code), .Res(regfile_1_p1));

  // Notes on the sheet:
  //   SHOULD AT LEAST WORK FOR ADD, ADDI AND MULT
  //   SET THIS TO 0 IF YOU DO NOT WANT TO OVERWRITE REGISTERS ... EX MULT -- HI AND LOW LIVE  IN THE ALU
  //   FOR MULT YOU DON'T WANT TO CHANGE ANY REGISTERS
  //   MULITPLEXER USED TO DETERMINE WHETHER IT IS I TYPE OR R TYPE
  //   BASICALLLY MAKE THIS = TO ZERO TO TAKE THE R TYPE 
  //   USE THIS TO EXTEND NON 32 BIT NUMBERS INTO SIGNED 32 BIT NUMBERS
  //   ALU DOES ALL OPERATIONS ON EVERY OP1 AND OP2 FROM THE REGISTERS -- HOWEVER YOU NEED TO SPECIFY WHICH ONE TO GET FROM THE ALU CODE
endmodule

module regfile (
  input  [31:0] rd_data,
  input  [4:0] rs,
  input  [4:0] rt,
  input  write_e,
  input  [4:0] rd,
  output [31:0] rs_data,
  output [31:0] rt_data
);

  wire clock_1_out, demultiplexer_1_out0, demultiplexer_1_out1, demultiplexer_1_out2, demultiplexer_1_out3,
       demultiplexer_1_out4, demultiplexer_1_out5, demultiplexer_1_out6, demultiplexer_1_out7,
       demultiplexer_1_out8, demultiplexer_1_out9, demultiplexer_1_out10, demultiplexer_1_out11,
       demultiplexer_1_out12, demultiplexer_1_out13, demultiplexer_1_out14, demultiplexer_1_out15,
       demultiplexer_1_out16, demultiplexer_1_out17, demultiplexer_1_out18, demultiplexer_1_out19,
       demultiplexer_1_out20, demultiplexer_1_out21, demultiplexer_1_out22, demultiplexer_1_out23,
       demultiplexer_1_out24, demultiplexer_1_out25, demultiplexer_1_out26, demultiplexer_1_out27,
       demultiplexer_1_out28, demultiplexer_1_out29, demultiplexer_1_out30, demultiplexer_1_out31;
  wire [31:0] Reg1_at_q, reg2_q, reg3_q, reg4_q, reg5_q, reg6_q, reg7_q, reg8_q, reg9_q, reg10_q, reg11_q,
       reg12_q, reg13_q, reg14_q, reg15_q, reg16_q, reg17_q, reg18_q, reg19_q, reg20_q, reg21_q, reg22_q,
       reg23_q, reg24_q, reg25_q, reg26_q, reg27_q, reg28_q, reg29_q, reg30_q, reg31_q, register_1_q;

  Demultiplexer #(.select(5)) demultiplexer_1 (
    .out0(demultiplexer_1_out0), .out1(demultiplexer_1_out1), .out2(demultiplexer_1_out2),
    .out3(demultiplexer_1_out3), .out4(demultiplexer_1_out4), .out5(demultiplexer_1_out5),
    .out6(demultiplexer_1_out6), .out7(demultiplexer_1_out7), .out8(demultiplexer_1_out8),
    .out9(demultiplexer_1_out9), .out10(demultiplexer_1_out10), .out11(demultiplexer_1_out11),
    .out12(demultiplexer_1_out12), .out13(demultiplexer_1_out13), .out14(demultiplexer_1_out14),
    .out15(demultiplexer_1_out15), .out16(demultiplexer_1_out16), .out17(demultiplexer_1_out17),
    .out18(demultiplexer_1_out18), .out19(demultiplexer_1_out19), .out20(demultiplexer_1_out20),
    .out21(demultiplexer_1_out21), .out22(demultiplexer_1_out22), .out23(demultiplexer_1_out23),
    .out24(demultiplexer_1_out24), .out25(demultiplexer_1_out25), .out26(demultiplexer_1_out26),
    .out27(demultiplexer_1_out27), .out28(demultiplexer_1_out28), .out29(demultiplexer_1_out29),
    .out30(demultiplexer_1_out30), .out31(demultiplexer_1_out31), .in(write_e), .sel(rd));
  Register #(.width(32)) Reg1_at (
    .D({32{1'b0}}), .en(demultiplexer_1_out0), .clk(clock_1_out), .Q(Reg1_at_q));  // open: clr
  Register #(.width(32)) register_1 (
    .D(rd_data), .en(demultiplexer_1_out1), .clk(clock_1_out), .Q(register_1_q));  // open: clr
  Register #(.width(32)) reg2 (.D(rd_data), .en(demultiplexer_1_out2), .clk(clock_1_out), .Q(reg2_q));  // open: clr
  Register #(.width(32)) reg3 (.D(rd_data), .en(demultiplexer_1_out3), .clk(clock_1_out), .Q(reg3_q));  // open: clr
  Register #(.width(32)) reg4 (.D(rd_data), .en(demultiplexer_1_out4), .clk(clock_1_out), .Q(reg4_q));  // open: clr
  Register #(.width(32)) reg5 (.D(rd_data), .en(demultiplexer_1_out5), .clk(clock_1_out), .Q(reg5_q));  // open: clr
  Register #(.width(32)) reg6 (.D(rd_data), .en(demultiplexer_1_out6), .clk(clock_1_out), .Q(reg6_q));  // open: clr
  Register #(.width(32)) reg7 (.D(rd_data), .en(demultiplexer_1_out7), .clk(clock_1_out), .Q(reg7_q));  // open: clr
  Register #(.width(32)) reg8 (.D(rd_data), .en(demultiplexer_1_out8), .clk(clock_1_out), .Q(reg8_q));  // open: clr
  Register #(.width(32)) reg9 (.D(rd_data), .en(demultiplexer_1_out9), .clk(clock_1_out), .Q(reg9_q));  // open: clr
  Register #(.width(32)) reg10 (.D(rd_data), .en(demultiplexer_1_out10), .clk(clock_1_out), .Q(reg10_q));  // open: clr
  Register #(.width(32)) reg11 (.D(rd_data), .en(demultiplexer_1_out11), .clk(clock_1_out), .Q(reg11_q));  // open: clr
  Register #(.width(32)) reg12 (.D(rd_data), .en(demultiplexer_1_out12), .clk(clock_1_out), .Q(reg12_q));  // open: clr
  Register #(.width(32)) reg13 (.D(rd_data), .en(demultiplexer_1_out13), .clk(clock_1_out), .Q(reg13_q));  // open: clr
  Clock clock_1 (.out(clock_1_out));
  Register #(.width(32)) reg14 (.D(rd_data), .en(demultiplexer_1_out14), .clk(clock_1_out), .Q(reg14_q));  // open: clr
  Register #(.width(32)) reg15 (.D(rd_data), .en(demultiplexer_1_out15), .clk(clock_1_out), .Q(reg15_q));  // open: clr
  Register #(.width(32)) reg16 (.D(rd_data), .en(demultiplexer_1_out16), .clk(clock_1_out), .Q(reg16_q));  // open: clr
  Register #(.width(32)) reg17 (.D(rd_data), .en(demultiplexer_1_out17), .clk(clock_1_out), .Q(reg17_q));  // open: clr
  Register #(.width(32)) reg18 (.D(rd_data), .en(demultiplexer_1_out18), .clk(clock_1_out), .Q(reg18_q));  // open: clr
  Register #(.width(32)) reg19 (.D(rd_data), .en(demultiplexer_1_out19), .clk(clock_1_out), .Q(reg19_q));  // open: clr
  Register #(.width(32)) reg20 (.D(rd_data), .en(demultiplexer_1_out20), .clk(clock_1_out), .Q(reg20_q));  // open: clr
  Register #(.width(32)) reg21 (.D(rd_data), .en(demultiplexer_1_out21), .clk(clock_1_out), .Q(reg21_q));  // open: clr
  Register #(.width(32)) reg22 (.D(rd_data), .en(demultiplexer_1_out22), .clk(clock_1_out), .Q(reg22_q));  // open: clr
  Register #(.width(32)) reg23 (.D(rd_data), .en(demultiplexer_1_out23), .clk(clock_1_out), .Q(reg23_q));  // open: clr
  Register #(.width(32)) reg24 (.D(rd_data), .en(demultiplexer_1_out24), .clk(clock_1_out), .Q(reg24_q));  // open: clr
  Register #(.width(32)) reg25 (.D(rd_data), .en(demultiplexer_1_out25), .clk(clock_1_out), .Q(reg25_q));  // open: clr
  Register #(.width(32)) reg26 (.D(rd_data), .en(demultiplexer_1_out26), .clk(clock_1_out), .Q(reg26_q));  // open: clr
  Register #(.width(32)) reg27 (.D(rd_data), .en(demultiplexer_1_out27), .clk(clock_1_out), .Q(reg27_q));  // open: clr
  Register #(.width(32)) reg28 (.D(rd_data), .en(demultiplexer_1_out28), .clk(clock_1_out), .Q(reg28_q));  // open: clr
  Register #(.width(32)) reg29 (.D(rd_data), .en(demultiplexer_1_out29), .clk(clock_1_out), .Q(reg29_q));  // open: clr
  Register #(.width(32)) reg30 (.D(rd_data), .en(demultiplexer_1_out30), .clk(clock_1_out), .Q(reg30_q));  // open: clr
  Register #(.width(32)) reg31 (.D(rd_data), .en(demultiplexer_1_out31), .clk(clock_1_out), .Q(reg31_q));  // open: clr
  Multiplexer #(.select(5), .width(32)) multiplexer_1 (
    .in0(Reg1_at_q), .in1(register_1_q), .in2(reg2_q), .in3(reg3_q), .in4(reg4_q), .in5(reg5_q),
    .in6(reg6_q), .in7(reg7_q), .in8(reg8_q), .in9(reg9_q), .in10(reg10_q), .in11(reg11_q), .in12(reg12_q),
    .in13(reg13_q), .in14(reg14_q), .in15(reg15_q), .in16(reg16_q), .in17(reg17_q), .in18(reg18_q),
    .in19(reg19_q), .in20(reg20_q), .in21(reg21_q), .in22(reg22_q), .in23(reg23_q), .in24(reg24_q),
    .in25(reg25_q), .in26(reg26_q), .in27(reg27_q), .in28(reg28_q), .in29(reg29_q), .in30(reg30_q),
    .in31(reg31_q), .out(rs_data), .sel(rs));
  Multiplexer #(.select(5), .width(32)) multiplexer_2 (
    .in0(Reg1_at_q), .in1(register_1_q), .in2(reg2_q), .in3(reg3_q), .in4(reg4_q), .in5(reg5_q),
    .in6(reg6_q), .in7(reg7_q), .in8(reg8_q), .in9(reg9_q), .in10(reg10_q), .in11(reg11_q), .in12(reg12_q),
    .in13(reg13_q), .in14(reg14_q), .in15(reg15_q), .in16(reg16_q), .in17(reg17_q), .in18(reg18_q),
    .in19(reg19_q), .in20(reg20_q), .in21(reg21_q), .in22(reg22_q), .in23(reg23_q), .in24(reg24_q),
    .in25(reg25_q), .in26(reg26_q), .in27(reg27_q), .in28(reg28_q), .in29(reg29_q), .in30(reg30_q),
    .in31(reg31_q), .out(rt_data), .sel(rt));

  // Notes on the sheet:
  //   reg1
  //   rs
endmodule

module ALU (
  input  [31:0] OP1,
  input  [31:0] OP2,
  input  [3:0] ALU_CODE,
  output [31:0] Res
);

  wire clock_1_out, comparator_1_gt, comparator_2_eq, comparator_3_eq, or_1_out;
  wire [31:0] adder_1_out, bit_extender_1_out, divider_1_out, divider_1_rem, HI_q, LO_q, multiplexer_2_out,
       multiplexer_3_out, multiplier_1_cout, multiplier_1_out, shifter_1_out, shifter_2_out, subtractor_1_out;

  Adder #(.width(32)) adder_1 (.a(OP1), .b(OP2), .out(adder_1_out));  // open: cin, cout
  Subtractor #(.width(32)) subtractor_1 (.a(OP1), .b(OP2), .out(subtractor_1_out));  // open: bin, bout
  Multiplier #(.width(32)) multiplier_1 (
    .a(OP1), .b(OP2), .out(multiplier_1_out), .cout(multiplier_1_cout));  // open: cin
  Divider #(.width(32)) divider_1 (.a(OP1), .b(OP2), .out(divider_1_out), .rem(divider_1_rem));  // open: upper
  Shifter #(.width(32)) shifter_1 (.in(OP1), .\dist (OP2[4:0]), .out(shifter_1_out));
  Shifter #(.shift("lr"), .width(32)) shifter_2 (.in(OP1), .\dist (OP2[4:0]), .out(shifter_2_out));
  Comparator #(.width(32)) comparator_1 (.a(OP1), .b(OP2), .gt(comparator_1_gt));  // open: eq, lt
  assign bit_extender_1_out = {{31{comparator_1_gt}}, comparator_1_gt};  // Bit_Extender bit_extender_1
  Multiplexer #(.select(4), .width(32)) multiplexer_1 (
    .in0(adder_1_out), .in1(subtractor_1_out), .in2(multiplier_1_out), .in3(divider_1_out), .in4(HI_q),
    .in5(LO_q), .in6(shifter_1_out), .in7(shifter_2_out), .in8(bit_extender_1_out), .in9({32{1'b0}}),
    .in10({32{1'b0}}), .in11({32{1'b0}}), .in12({32{1'b0}}), .in13({32{1'b0}}), .in14({32{1'b0}}),
    .in15({32{1'b0}}), .out(Res), .sel(ALU_CODE));
  Comparator #(.width(4)) comparator_2 (.a(4'b0010), .b(ALU_CODE), .eq(comparator_2_eq));  // open: gt, lt
  Comparator #(.width(4)) comparator_3 (.a(4'b0011), .b(ALU_CODE), .eq(comparator_3_eq));  // open: gt, lt
  Multiplexer #(.width(32)) multiplexer_2 (
    .in0(multiplier_1_cout), .in1(divider_1_out), .out(multiplexer_2_out), .sel(comparator_3_eq));
  Multiplexer #(.width(32)) multiplexer_3 (
    .in0(multiplier_1_out), .in1(divider_1_rem), .out(multiplexer_3_out), .sel(comparator_3_eq));
  or or_1 (or_1_out, comparator_2_eq, comparator_3_eq);
  Register #(.width(32)) HI (.D(multiplexer_2_out), .en(or_1_out), .clk(clock_1_out), .Q(HI_q));  // open: clr
  Register #(.width(32)) LO (.D(multiplexer_3_out), .en(or_1_out), .clk(clock_1_out), .Q(LO_q));  // open: clr
  Clock clock_1 (.out(clock_1_out));

  // Notes on the sheet:
  //   I HAVE UPDATED THIS A LOT.... REVERT TO OTHER ONE FOR THE SETUP JUST FROM CLASS
  //   these are shifts will have to check them
  //   breaking it into 5 bits and 27 bits cause it doesnt seem to work past 5 with the shifter? figure out how this works better
  //   thinking about what we have to do.... if the ALU code is anything but mult or divide we take the outputs and output them... if it is div or mult we dont output anything but instead store values into HI or LO
  //   pretty sure this works cause div and mult are made to not change the Res in the main?
  //   THIS IS NOT DONE I HAVE NO IDEA HOW TO GET THE REMAINDER
endmodule

module Control (
  input  [31:0] Inst,
  output [4:0] rs,
  output [4:0] rt,
  output [4:0] rd,
  output [31:0] imm,
  output reg_write_e,
  output imm_sel,
  output [3:0] ALU_code
);

  Bit_Extender bit_extender_1 ();  // open: in, out

  // Notes on the sheet:
  //   USE THIS TO RETURN ONLY 32 BIT NUMBERS AND TO EXTEND IT
endmodule

module ignore (
  input  [31:0] in_1,
  input  [31:0] in_2
);

  wire control_1_imm_sel, control_2_imm_sel, multiplexer_1_out, multiplexer_3_out, regfile_1_p2,
       regfile_2_p2, undriven, undriven_2, undriven_3, undriven_4;
  wire [3:0] control_1_alu_code, control_2_alu_code;
  wire [4:0] regfile_1_p3, regfile_1_p4, regfile_1_p5, regfile_2_p3, regfile_2_p4, regfile_2_p5;
  wire [31:0] alu_1_res, alu_2_res, control_1_imm, control_2_imm, multiplexer_2_out, multiplexer_4_out,
       regfile_1_p6, regfile_1_p7, regfile_2_p6, regfile_2_p7;

  Multiplexer multiplexer_1 (.in0(alu_1_res[0]), .in1(undriven), .out(multiplexer_1_out), .sel(undriven_2));
  // regfile regfile_1: pin names not known; wires that end beside it: multiplexer_1_out, regfile_1_p2, regfile_1_p3, regfile_1_p4, regfile_1_p5, regfile_1_p6, regfile_1_p7
  Control control_1 (
    .Inst(in_1), .rs(regfile_1_p4), .rt(regfile_1_p5), .rd(regfile_1_p3), .imm(control_1_imm),
    .reg_write_e(regfile_1_p2), .imm_sel(control_1_imm_sel), .ALU_code(control_1_alu_code));
  Multiplexer #(.width(32)) multiplexer_2 (
    .in0(regfile_1_p7), .in1(control_1_imm), .out(multiplexer_2_out), .sel(control_1_imm_sel));
  ALU alu_1 (.OP2(multiplexer_2_out), .OP1(regfile_1_p6), .ALU_CODE(control_1_alu_code), .Res(alu_1_res));
  Multiplexer multiplexer_3 (.in0(alu_2_res[0]), .in1(undriven_4), .out(multiplexer_3_out), .sel(undriven_3));
  // regfile regfile_2: pin names not known; wires that end beside it: multiplexer_3_out, regfile_2_p2, regfile_2_p3, regfile_2_p4, regfile_2_p5, regfile_2_p6, regfile_2_p7
  Control control_2 (
    .Inst(in_2), .rs(regfile_2_p4), .rt(regfile_2_p5), .rd(regfile_2_p3), .imm(control_2_imm),
    .reg_write_e(regfile_2_p2), .imm_sel(control_2_imm_sel), .ALU_code(control_2_alu_code));
  Multiplexer #(.width(32)) multiplexer_4 (
    .in0(regfile_2_p7), .in1(control_2_imm), .out(multiplexer_4_out), .sel(control_2_imm_sel));
  ALU alu_2 (.OP2(multiplexer_4_out), .OP1(regfile_2_p6), .ALU_CODE(control_2_alu_code), .Res(alu_2_res));
  // Pins of 1 and 32 bits meet at alu_2_res
  // Pins of 1 and 32 bits meet at alu_1_res

  // Notes on the sheet:
  //   lw $t0, 4($t1)
  //   new control outputs
  //   new output
  //   t1
  //   read ram
  //   4
  //   we need the immediate to be the offset for ram
  //   add
  //   add ram reading functionality
  //   new ALU codes
  //   false
  //   ram write enable
  //   ram output
  //   ram read in as well as shifter and bit extender (making it word readable)
  //   sw $t0, 4($t1)
  //   new control outputs
  //   new output
  //   t1
  //   t0
  //   read ram
  //   4
  //   we need the immediate to be the offset for ram
  //   add
  //   new ALU codes
  //   add ram reading functionality
  //   true
  //   ram write enable
  //   ram output
  //   ram read in as well as shifter and bit extender (making it word readable)
  //   ram input register part
endmodule
